// Logisim project Lab2.circ as structural Verilog: 3 circuits, main circuit main
module main (
  input  [31:0] in_1,
  input  [31:0] in_2,
  input  [31:0] in_3,
  input  [3:0] ALU_Control,
  input  [31:0] in_5,
  output [31:0] out_6,
  output [31:0] out_7,
  output ZERO,
  output OVERFLOW,
  output CARRYOUT,
  output NEGATIVE
);

  ALU64bit alu64bit_1 (
    .in_1(in_1), .in_2(in_2), .in_3(in_3), .in_4(in_5), .Cout(CARRYOUT), .out_7(out_6), .out_8(out_7),
    .Overflow(OVERFLOW), .Zero(ZERO), .in_5(ALU_Control), .out_6(NEGATIVE));

  // Notes on the sheet:
  //   Bus A
  //   Bus B
  //   ALU 64 bit
  //   Output
endmodule

module ALU64bit (
  input  [31:0] in_1,
  input  [31:0] in_2,
  input  [31:0] in_3,
  input  [31:0] in_4,
  input  [3:0] in_5,
  output out_6,
  output [31:0] out_7,
  output [31:0] out_8,
  output Overflow,
  output Zero,
  output Cout
);

  wire alu1bit_1_cout, alu1bit_2_cout, alu1bit_3_cout, alu1bit_4_cout, alu1bit_5_cout, alu1bit_6_cout,
       alu1bit_7_cout, alu1bit_8_cout, alu1bit_9_cout, alu1bit_10_cout, alu1bit_11_cout, alu1bit_12_cout,
       alu1bit_13_cout, alu1bit_14_cout, alu1bit_15_cout, alu1bit_16_cout, alu1bit_17_cout, alu1bit_18_cout,
       alu1bit_19_cout, alu1bit_20_cout, alu1bit_21_cout, alu1bit_22_cout, alu1bit_23_cout, alu1bit_24_cout,
       alu1bit_25_cout, alu1bit_26_cout, alu1bit_27_cout, alu1bit_28_cout, alu1bit_29_cout, alu1bit_30_cout,
       alu1bit_31_cout, alu1bit_32_cout, alu1bit_33_cout, alu1bit_34_cout, alu1bit_35_cout, alu1bit_36_cout,
       alu1bit_37_cout, alu1bit_38_cout, alu1bit_39_cout, alu1bit_40_cout, alu1bit_41_cout, alu1bit_42_cout,
       alu1bit_43_cout, alu1bit_44_cout, alu1bit_45_cout, alu1bit_46_cout, alu1bit_47_cout, alu1bit_48_cout,
       alu1bit_49_cout, alu1bit_50_cout, alu1bit_51_cout, alu1bit_52_cout, alu1bit_53_cout, alu1bit_54_cout,
       alu1bit_55_cout, alu1bit_56_cout, alu1bit_57_cout, alu1bit_58_cout, alu1bit_59_cout, alu1bit_60_cout,
       alu1bit_61_cout, alu1bit_62_cout, alu1bit_63_cout, or_1_out, or_2_out;

  ALU1bit alu1bit_1 (
    .A(in_2[0]), .B(in_4[0]), .Cin(in_5[2]), .Cout(alu1bit_1_cout), .Binvert(in_5[2]), .in_4(in_5[1:0]),
    .C(out_8[0]));
  ALU1bit alu1bit_2 (
    .A(in_2[1]), .B(in_4[1]), .Cin(alu1bit_1_cout), .Cout(alu1bit_2_cout), .Binvert(in_5[2]),
    .in_4(in_5[1:0]), .C(out_8[1]));
  ALU1bit alu1bit_3 (
    .A(in_2[2]), .B(in_4[2]), .Cin(alu1bit_2_cout), .Cout(alu1bit_3_cout), .Binvert(in_5[2]),
    .in_4(in_5[1:0]), .C(out_8[2]));
  ALU1bit alu1bit_4 (
    .A(in_2[3]), .B(in_4[3]), .Cin(alu1bit_3_cout), .Cout(alu1bit_4_cout), .Binvert(in_5[2]),
    .in_4(in_5[1:0]), .C(out_8[3]));
  ALU1bit alu1bit_5 (
    .A(in_2[4]), .B(in_4[4]), .Cin(alu1bit_4_cout), .Cout(alu1bit_5_cout), .Binvert(in_5[2]),
    .in_4(in_5[1:0]), .C(out_8[4]));
  ALU1bit alu1bit_6 (
    .A(in_2[5]), .B(in_4[5]), .Cin(alu1bit_5_cout), .Cout(alu1bit_6_cout), .Binvert(in_5[2]),
    .in_4(in_5[1:0]), .C(out_8[5]));
  ALU1bit alu1bit_7 (
    .A(in_2[6]), .B(in_4[6]), .Cin(alu1bit_6_cout), .Cout(alu1bit_7_cout), .Binvert(in_5[2]),
    .in_4(in_5[1:0]), .C(out_8[6]));
  ALU1bit alu1bit_8 (
    .A(in_2[7]), .B(in_4[7]), .Cin(alu1bit_7_cout), .Cout(alu1bit_8_cout), .Binvert(in_5[2]),
    .in_4(in_5[1:0]), .C(out_8[7]));
  ALU1bit alu1bit_9 (
    .A(in_2[8]), .B(in_4[8]), .Cin(alu1bit_8_cout), .Cout(alu1bit_9_cout), .Binvert(in_5[2]),
    .in_4(in_5[1:0]), .C(out_8[8]));
  ALU1bit alu1bit_10 (
    .A(in_2[9]), .B(in_4[9]), .Cin(alu1bit_9_cout), .Cout(alu1bit_10_cout), .Binvert(in_5[2]),
    .in_4(in_5[1:0]), .C(out_8[9]));
  ALU1bit alu1bit_11 (
    .A(in_2[10]), .B(in_4[10]), .Cin(alu1bit_10_cout), .Cout(alu1bit_11_cout), .Binvert(in_5[2]),
    .in_4(in_5[1:0]), .C(out_8[10]));
  ALU1bit alu1bit_12 (
    .A(in_2[11]), .B(in_4[11]), .Cin(alu1bit_11_cout), .Cout(alu1bit_12_cout), .Binvert(in_5[2]),
    .in_4(in_5[1:0]), .C(out_8[11]));
  ALU1bit alu1bit_13 (
    .A(in_2[12]), .B(in_4[12]), .Cin(alu1bit_12_cout), .Cout(alu1bit_13_cout), .Binvert(in_5[2]),
    .in_4(in_5[1:0]), .C(out_8[12]));
  ALU1bit alu1bit_14 (
    .A(in_2[13]), .B(in_4[13]), .Cin(alu1bit_13_cout), .Cout(alu1bit_14_cout), .Binvert(in_5[2]),
    .in_4(in_5[1:0]), .C(out_8[13]));
  ALU1bit alu1bit_15 (
    .A(in_2[14]), .B(in_4[14]), .Cin(alu1bit_14_cout), .Cout(alu1bit_15_cout), .Binvert(in_5[2]),
    .in_4(in_5[1:0]), .C(out_8[14]));
  ALU1bit alu1bit_16 (
    .A(in_2[15]), .B(in_4[15]), .Cin(alu1bit_15_cout), .Cout(alu1bit_16_cout), .Binvert(in_5[2]),
    .in_4(in_5[1:0]), .C(out_8[15]));
  ALU1bit alu1bit_17 (
    .A(in_2[16]), .B(in_4[16]), .Cin(alu1bit_16_cout), .Cout(alu1bit_17_cout), .Binvert(in_5[2]),
    .in_4(in_5[1:0]), .C(out_8[16]));
  ALU1bit alu1bit_18 (
    .A(in_2[17]), .B(in_4[17]), .Cin(alu1bit_17_cout), .Cout(alu1bit_18_cout), .Binvert(in_5[2]),
    .in_4(in_5[1:0]), .C(out_8[17]));
  ALU1bit alu1bit_19 (
    .A(in_2[18]), .B(in_4[18]), .Cin(alu1bit_18_cout), .Cout(alu1bit_19_cout), .Binvert(in_5[2]),
    .in_4(in_5[1:0]), .C(out_8[18]));
  ALU1bit alu1bit_20 (
    .A(in_2[19]), .B(in_4[19]), .Cin(alu1bit_19_cout), .Cout(alu1bit_20_cout), .Binvert(in_5[2]),
    .in_4(in_5[1:0]), .C(out_8[19]));
  ALU1bit alu1bit_21 (
    .A(in_2[20]), .B(in_4[20]), .Cin(alu1bit_20_cout), .Cout(alu1bit_21_cout), .Binvert(in_5[2]),
    .in_4(in_5[1:0]), .C(out_8[20]));
  ALU1bit alu1bit_22 (
    .A(in_2[21]), .B(in_4[21]), .Cin(alu1bit_21_cout), .Cout(alu1bit_22_cout), .Binvert(in_5[2]),
    .in_4(in_5[1:0]), .C(out_8[21]));
  ALU1bit alu1bit_23 (
    .A(in_2[22]), .B(in_4[22]), .Cin(alu1bit_22_cout), .Cout(alu1bit_23_cout), .Binvert(in_5[2]),
    .in_4(in_5[1:0]), .C(out_8[22]));
  ALU1bit alu1bit_24 (
    .A(in_2[23]), .B(in_4[23]), .Cin(alu1bit_23_cout), .Cout(alu1bit_24_cout), .Binvert(in_5[2]),
    .in_4(in_5[1:0]), .C(out_8[23]));
  ALU1bit alu1bit_25 (
    .A(in_2[24]), .B(in_4[24]), .Cin(alu1bit_24_cout), .Cout(alu1bit_25_cout), .Binvert(in_5[2]),
    .in_4(in_5[1:0]), .C(out_8[24]));
  ALU1bit alu1bit_26 (
    .A(in_2[25]), .B(in_4[25]), .Cin(alu1bit_25_cout), .Cout(alu1bit_26_cout), .Binvert(in_5[2]),
    .in_4(in_5[1:0]), .C(out_8[25]));
  ALU1bit alu1bit_27 (
    .A(in_2[26]), .B(in_4[26]), .Cin(alu1bit_26_cout), .Cout(alu1bit_27_cout), .Binvert(in_5[2]),
    .in_4(in_5[1:0]), .C(out_8[26]));
  ALU1bit alu1bit_28 (
    .A(in_2[27]), .B(in_4[27]), .Cin(alu1bit_27_cout), .Cout(alu1bit_28_cout), .Binvert(in_5[2]),
    .in_4(in_5[1:0]), .C(out_8[27]));
  ALU1bit alu1bit_29 (
    .A(in_2[28]), .B(in_4[28]), .Cin(alu1bit_28_cout), .Cout(alu1bit_29_cout), .Binvert(in_5[2]),
    .in_4(in_5[1:0]), .C(out_8[28]));
  ALU1bit alu1bit_30 (
    .A(in_2[29]), .B(in_4[29]), .Cin(alu1bit_29_cout), .Cout(alu1bit_30_cout), .Binvert(in_5[2]),
    .in_4(in_5[1:0]), .C(out_8[29]));
  ALU1bit alu1bit_31 (
    .A(in_2[30]), .B(in_4[30]), .Cin(alu1bit_30_cout), .Cout(alu1bit_31_cout), .Binvert(in_5[2]),
    .in_4(in_5[1:0]), .C(out_8[30]));
  ALU1bit alu1bit_32 (
    .A(in_2[31]), .B(in_4[31]), .Cin(alu1bit_31_cout), .Cout(alu1bit_32_cout), .Binvert(in_5[2]),
    .in_4(in_5[1:0]), .C(out_8[31]));
  ALU1bit alu1bit_33 (
    .A(in_1[0]), .B(in_3[0]), .Cin(alu1bit_32_cout), .Cout(alu1bit_33_cout), .Binvert(in_5[2]),
    .in_4(in_5[1:0]), .C(out_7[0]));
  ALU1bit alu1bit_34 (
    .A(in_1[1]), .B(in_3[1]), .Cin(alu1bit_33_cout), .Cout(alu1bit_34_cout), .Binvert(in_5[2]),
    .in_4(in_5[1:0]), .C(out_7[1]));
  ALU1bit alu1bit_35 (
    .A(in_1[2]), .B(in_3[2]), .Cin(alu1bit_34_cout), .Cout(alu1bit_35_cout), .Binvert(in_5[2]),
    .in_4(in_5[1:0]), .C(out_7[2]));
  ALU1bit alu1bit_36 (
    .A(in_1[3]), .B(in_3[3]), .Cin(alu1bit_35_cout), .Cout(alu1bit_36_cout), .Binvert(in_5[2]),
    .in_4(in_5[1:0]), .C(out_7[3]));
  ALU1bit alu1bit_37 (
    .A(in_1[4]), .B(in_3[4]), .Cin(alu1bit_36_cout), .Cout(alu1bit_37_cout), .Binvert(in_5[2]),
    .in_4(in_5[1:0]), .C(out_7[4]));
  ALU1bit alu1bit_38 (
    .A(in_1[5]), .B(in_3[5]), .Cin(alu1bit_37_cout), .Cout(alu1bit_38_cout), .Binvert(in_5[2]),
    .in_4(in_5[1:0]), .C(out_7[5]));
  ALU1bit alu1bit_39 (
    .A(in_1[6]), .B(in_3[6]), .Cin(alu1bit_38_cout), .Cout(alu1bit_39_cout), .Binvert(in_5[2]),
    .in_4(in_5[1:0]), .C(out_7[6]));
  ALU1bit alu1bit_40 (
    .A(in_1[7]), .B(in_3[7]), .Cin(alu1bit_39_cout), .Cout(alu1bit_40_cout), .Binvert(in_5[2]),
    .in_4(in_5[1:0]), .C(out_7[7]));
  ALU1bit alu1bit_41 (
    .A(in_1[8]), .B(in_3[8]), .Cin(alu1bit_40_cout), .Cout(alu1bit_41_cout), .Binvert(in_5[2]),
    .in_4(in_5[1:0]), .C(out_7[8]));
  ALU1bit alu1bit_42 (
    .A(in_1[9]), .B(in_3[9]), .Cin(alu1bit_41_cout), .Cout(alu1bit_42_cout), .Binvert(in_5[2]),
    .in_4(in_5[1:0]), .C(out_7[9]));
  ALU1bit alu1bit_43 (
    .A(in_1[10]), .B(in_3[10]), .Cin(alu1bit_42_cout), .Cout(alu1bit_43_cout), .Binvert(in_5[2]),
    .in_4(in_5[1:0]), .C(out_7[10]));
  ALU1bit alu1bit_44 (
    .A(in_1[11]), .B(in_3[11]), .Cin(alu1bit_43_cout), .Cout(alu1bit_44_cout), .Binvert(in_5[2]),
    .in_4(in_5[1:0]), .C(out_7[11]));
  ALU1bit alu1bit_45 (
    .A(in_1[12]), .B(in_3[12]), .Cin(alu1bit_44_cout), .Cout(alu1bit_45_cout), .Binvert(in_5[2]),
    .in_4(in_5[1:0]), .C(out_7[12]));
  ALU1bit alu1bit_46 (
    .A(in_1[13]), .B(in_3[13]), .Cin(alu1bit_45_cout), .Cout(alu1bit_46_cout), .Binvert(in_5[2]),
    .in_4(in_5[1:0]), .C(out_7[13]));
  ALU1bit alu1bit_47 (
    .A(in_1[14]), .B(in_3[14]), .Cin(alu1bit_46_cout), .Cout(alu1bit_47_cout), .Binvert(in_5[2]),
    .in_4(in_5[1:0]), .C(out_7[14]));
  ALU1bit alu1bit_48 (
    .A(in_1[15]), .B(in_3[15]), .Cin(alu1bit_47_cout), .Cout(alu1bit_48_cout), .Binvert(in_5[2]),
    .in_4(in_5[1:0]), .C(out_7[15]));
  ALU1bit alu1bit_49 (
    .A(in_1[16]), .B(in_3[16]), .Cin(alu1bit_48_cout), .Cout(alu1bit_49_cout), .Binvert(in_5[2]),
    .in_4(in_5[1:0]), .C(out_7[16]));
  ALU1bit alu1bit_50 (
    .A(in_1[17]), .B(in_3[17]), .Cin(alu1bit_49_cout), .Cout(alu1bit_50_cout), .Binvert(in_5[2]),
    .in_4(in_5[1:0]), .C(out_7[17]));
  ALU1bit alu1bit_51 (
    .A(in_1[18]), .B(in_3[18]), .Cin(alu1bit_50_cout), .Cout(alu1bit_51_cout), .Binvert(in_5[2]),
    .in_4(in_5[1:0]), .C(out_7[18]));
  ALU1bit alu1bit_52 (
    .A(in_1[19]), .B(in_3[19]), .Cin(alu1bit_51_cout), .Cout(alu1bit_52_cout), .Binvert(in_5[2]),
    .in_4(in_5[1:0]), .C(out_7[19]));
  ALU1bit alu1bit_53 (
    .A(in_1[20]), .B(in_3[20]), .Cin(alu1bit_52_cout), .Cout(alu1bit_53_cout), .Binvert(in_5[2]),
    .in_4(in_5[1:0]), .C(out_7[20]));
  ALU1bit alu1bit_54 (
    .A(in_1[21]), .B(in_3[21]), .Cin(alu1bit_53_cout), .Cout(alu1bit_54_cout), .Binvert(in_5[2]),
    .in_4(in_5[1:0]), .C(out_7[21]));
  ALU1bit alu1bit_55 (
    .A(in_1[22]), .B(in_3[22]), .Cin(alu1bit_54_cout), .Cout(alu1bit_55_cout), .Binvert(in_5[2]),
    .in_4(in_5[1:0]), .C(out_7[22]));
  ALU1bit alu1bit_56 (
    .A(in_1[23]), .B(in_3[23]), .Cin(alu1bit_55_cout), .Cout(alu1bit_56_cout), .Binvert(in_5[2]),
    .in_4(in_5[1:0]), .C(out_7[23]));
  ALU1bit alu1bit_57 (
    .A(in_1[24]), .B(in_3[24]), .Cin(alu1bit_56_cout), .Cout(alu1bit_57_cout), .Binvert(in_5[2]),
    .in_4(in_5[1:0]), .C(out_7[24]));
  ALU1bit alu1bit_58 (
    .A(in_1[25]), .B(in_3[25]), .Cin(alu1bit_57_cout), .Cout(alu1bit_58_cout), .Binvert(in_5[2]),
    .in_4(in_5[1:0]), .C(out_7[25]));
  ALU1bit alu1bit_59 (
    .A(in_1[26]), .B(in_3[26]), .Cin(alu1bit_58_cout), .Cout(alu1bit_59_cout), .Binvert(in_5[2]),
    .in_4(in_5[1:0]), .C(out_7[26]));
  ALU1bit alu1bit_60 (
    .A(in_1[27]), .B(in_3[27]), .Cin(alu1bit_59_cout), .Cout(alu1bit_60_cout), .Binvert(in_5[2]),
    .in_4(in_5[1:0]), .C(out_7[27]));
  ALU1bit alu1bit_61 (
    .A(in_1[28]), .B(in_3[28]), .Cin(alu1bit_60_cout), .Cout(alu1bit_61_cout), .Binvert(in_5[2]),
    .in_4(in_5[1:0]), .C(out_7[28]));
  ALU1bit alu1bit_62 (
    .A(in_1[29]), .B(in_3[29]), .Cin(alu1bit_61_cout), .Cout(alu1bit_62_cout), .Binvert(in_5[2]),
    .in_4(in_5[1:0]), .C(out_7[29]));
  ALU1bit alu1bit_63 (
    .A(in_1[30]), .B(in_3[30]), .Cin(alu1bit_62_cout), .Cout(alu1bit_63_cout), .Binvert(in_5[2]),
    .in_4(in_5[1:0]), .C(out_7[30]));
  ALU1bit alu1bit_64 (
    .A(in_1[31]), .B(in_3[31]), .Cin(alu1bit_63_cout), .Cout(Cout), .Binvert(in_5[2]), .in_4(in_5[1:0]),
    .C(out_6));
  xor xor_1 (Overflow, alu1bit_63_cout, Cout);
  or or_1 (or_1_out, out_7[0], out_7[1], out_7[2], out_7[3], out_7[4], out_7[5], out_7[6], out_7[7], out_7[8], out_7[9], out_7[10], out_7[11], out_7[12], out_7[13], out_7[14], out_7[15], out_7[16], out_7[17], out_7[18], out_7[19], out_7[20], out_7[21], out_7[22], out_7[23], out_7[24], out_7[25], out_7[26], out_7[27], out_7[28], out_7[29], out_7[30], out_6);
  or or_2 (or_2_out, out_8[0], out_8[1], out_8[2], out_8[3], out_8[4], out_8[5], out_8[6], out_8[7], out_8[8], out_8[9], out_8[10], out_8[11], out_8[12], out_8[13], out_8[14], out_8[15], out_8[16], out_8[17], out_8[18], out_8[19], out_8[20], out_8[21], out_8[22], out_8[23], out_8[24], out_8[25], out_8[26], out_8[27], out_8[28], out_8[29], out_8[30], out_8[31]);
  nor nor_1 (Zero, or_1_out, or_2_out);

  assign out_7[31] = out_6;

  // Other names for the same wires on the sheet: A32 = in_1[0]; A33 = in_1[1]; A34 = in_1[2]; A35 = in_1[3];
  //   A36 = in_1[4]; A37 = in_1[5]; A38 = in_1[6]; A39 = in_1[7]; A40 = in_1[8]; A41 = in_1[9]; A42 = in_1[10];
  //   A43 = in_1[11]; A44 = in_1[12]; A45 = in_1[13]; A46 = in_1[14]; A47 = in_1[15]; A48 = in_1[16]; A49 = in_1[17];
  //   A50 = in_1[18]; A51 = in_1[19]; A52 = in_1[20]; A53 = in_1[21]; A54 = in_1[22]; A55 = in_1[23]; A56 = in_1[24];
  //   A57 = in_1[25]; A58 = in_1[26]; A59 = in_1[27]; A60 = in_1[28]; A61 = in_1[29]; A62 = in_1[30]; A63 = in_1[31];
  //   A0 = in_2[0]; A1 = in_2[1]; A2 = in_2[2]; A3 = in_2[3]; A4 = in_2[4]; A5 = in_2[5]; A6 = in_2[6]; A7 = in_2[7];
  //   A8 = in_2[8]; A9 = in_2[9]; A10 = in_2[10]; A11 = in_2[11]; A12 = in_2[12]; A13 = in_2[13]; A14 = in_2[14];
  //   A15 = in_2[15]; A16 = in_2[16]; A17 = in_2[17]; A18 = in_2[18]; A19 = in_2[19]; A20 = in_2[20]; A21 = in_2[21];
  //   A22 = in_2[22]; A23 = in_2[23]; A24 = in_2[24]; A25 = in_2[25]; A26 = in_2[26]; A27 = in_2[27]; A28 = in_2[28];
  //   A29 = in_2[29]; A30 = in_2[30]; A31 = in_2[31]; B32 = in_3[0]; B33 = in_3[1]; B34 = in_3[2]; B35 = in_3[3];
  //   B36 = in_3[4]; B37 = in_3[5]; B38 = in_3[6]; B39 = in_3[7]; B40 = in_3[8]; B41 = in_3[9]; B42 = in_3[10];
  //   B43 = in_3[11]; B44 = in_3[12]; B45 = in_3[13]; B46 = in_3[14]; B47 = in_3[15]; B48 = in_3[16]; B49 = in_3[17];
  //   B50 = in_3[18]; B51 = in_3[19]; B52 = in_3[20]; B53 = in_3[21]; B54 = in_3[22]; B55 = in_3[23]; B56 = in_3[24];
  //   B57 = in_3[25]; B58 = in_3[26]; B59 = in_3[27]; B60 = in_3[28]; B61 = in_3[29]; B62 = in_3[30]; B63 = in_3[31];
  //   B0 = in_4[0]; B1 = in_4[1]; B2 = in_4[2]; B3 = in_4[3]; B4 = in_4[4]; B5 = in_4[5]; B6 = in_4[6]; B7 = in_4[7];
  //   B8 = in_4[8]; B9 = in_4[9]; B10 = in_4[10]; B11 = in_4[11]; B12 = in_4[12]; B13 = in_4[13]; B14 = in_4[14];
  //   B15 = in_4[15]; B16 = in_4[16]; B17 = in_4[17]; B18 = in_4[18]; B19 = in_4[19]; B20 = in_4[20]; B21 = in_4[21];
  //   B22 = in_4[22]; B23 = in_4[23]; B24 = in_4[24]; B25 = in_4[25]; B26 = in_4[26]; B27 = in_4[27]; B28 = in_4[28];
  //   B29 = in_4[29]; B30 = in_4[30]; B31 = in_4[31]; C32 = out_7[0]; C33 = out_7[1]; C34 = out_7[2]; C35 = out_7[3];
  //   C36 = out_7[4]; C37 = out_7[5]; C38 = out_7[6]; C39 = out_7[7]; C40 = out_7[8]; C41 = out_7[9]; C42 = out_7[10];
  //   C43 = out_7[11]; C44 = out_7[12]; C45 = out_7[13]; C46 = out_7[14]; C47 = out_7[15]; C48 = out_7[16];
  //   C49 = out_7[17]; C50 = out_7[18]; C51 = out_7[19]; C52 = out_7[20]; C53 = out_7[21]; C54 = out_7[22];
  //   C55 = out_7[23]; C56 = out_7[24]; C57 = out_7[25]; C58 = out_7[26]; C59 = out_7[27]; C60 = out_7[28];
  //   C61 = out_7[29]; C62 = out_7[30]; C63 = out_6; C0 = out_8[0]; C1 = out_8[1]; C2 = out_8[2]; C3 = out_8[3];
  //   C4 = out_8[4]; C5 = out_8[5]; C6 = out_8[6]; C7 = out_8[7]; C8 = out_8[8]; C9 = out_8[9]; C10 = out_8[10];
  //   C11 = out_8[11]; C12 = out_8[12]; C13 = out_8[13]; C14 = out_8[14]; C15 = out_8[15]; C16 = out_8[16];
  //   C17 = out_8[17]; C18 = out_8[18]; C19 = out_8[19]; C20 = out_8[20]; C21 = out_8[21]; C22 = out_8[22];
  //   C23 = out_8[23]; C24 = out_8[24]; C25 = out_8[25]; C26 = out_8[26]; C27 = out_8[27]; C28 = out_8[28];
  //   C29 = out_8[29]; C30 = out_8[30]; C31 = out_8[31]
endmodule

module ALU1bit (
  input  A,
  input  B,
  input  Cin,
  input  [1:0] in_4,
  input  Binvert,
  output C,
  output Cout
);

  wire adder_1_out, and_1_out, multiplexer_1_out, not_1_out, or_1_out;

  Multiplexer multiplexer_1 (.in0(B), .in1(not_1_out), .out(multiplexer_1_out), .sel(Binvert));  // open: en
  not not_1 (not_1_out, B);
  and and_1 (and_1_out, A, B);
  or or_1 (or_1_out, A, B);
  Adder #(.width(1)) adder_1 (.a(A), .b(multiplexer_1_out), .out(adder_1_out), .cin(Cin), .cout(Cout));
  Multiplexer #(.select(2)) multiplexer_2 (
    .in0(and_1_out), .in1(or_1_out), .in2(adder_1_out), .out(C), .sel(in_4));  // open: in3, en
endmodule
